# Fritzing sketch schematics (saved by Fritzing 0.9.3b)
breadboards: 1

parts:
  YwRobot_Power_Supply1 = YwRobot Breadboard Power Supply [part_number=545043]
  LPD8806_RGB_LED_Strip1 = LPD8806 RGB LED Strip
  Raspberry_Pi_1 = Raspberry Pi 3 [part_number=RPI-3-V1.2]

nets:
  N1: YwRobot_Power_Supply1.VCC#9, LPD8806_RGB_LED_Strip1.+5V
  GND: YwRobot_Power_Supply1.GND#13, LPD8806_RGB_LED_Strip1.GND, LPD8806_RGB_LED_Strip1.DI, Raspberry_Pi_1.GIPO10, Raspberry_Pi_1.GND, Raspberry_Pi_1.GIPO25
  N2: LPD8806_RGB_LED_Strip1.CI, Raspberry_Pi_1.GIPO11, Raspberry_Pi_1.GIPO8

custom parts:
  YwRobot Breadboard Power Supply: The YwRobot Breadboard Power Supply (MB-V2) has two power rails; they can be 5V or 3V3. Power to the module can be provided through the female USB socket or through the A10 (female) 2.1mm power jack.
  LPD8806 RGB LED Strip: Digitally addressable RGB LED strip
